// Digital circuit decodeur.dig as structural Verilog
module decodeur (
  input  [5:0] e,
  input  en,
  output _0,
  output _2,
  output _3,
  output _4,
  output _5,
  output _6,
  output _7,
  output _8,
  output _9,
  output _10,
  output _11,
  output _12,
  output _13,
  output _14,
  output _15,
  output _16,
  output _18,
  output _24,
  output _25,
  output _26,
  output _27,
  output _32,
  output _33,
  output _34,
  output _35,
  output _36,
  output _37,
  output _38,
  output _39,
  output _40,
  output _42,
  output _43
);

  wire not_1_out, not_2_out, not_3_out, not_4_out, not_5_out, not_6_out, not_7_out, not_8_out, not_9_out,
       not_10_out, not_11_out, not_12_out, not_13_out, not_14_out, not_15_out, not_16_out, not_17_out,
       not_18_out, not_19_out, not_20_out, not_21_out, not_22_out, not_23_out, not_24_out, not_25_out,
       not_26_out, not_27_out, not_28_out, not_29_out, not_30_out, not_31_out, not_32_out, not_33_out,
       not_34_out, not_35_out, not_36_out, not_37_out, not_38_out, not_39_out, not_40_out, not_41_out,
       not_42_out, not_43_out, not_44_out, not_45_out, not_46_out, not_47_out, not_48_out, not_49_out,
       not_50_out, not_51_out, not_52_out, not_53_out, not_54_out, not_55_out, not_56_out, not_57_out,
       not_58_out, not_59_out, not_60_out, not_61_out, not_62_out, not_63_out, not_64_out, not_65_out,
       not_66_out, not_67_out, not_68_out, not_69_out, not_70_out, not_71_out, not_72_out, not_73_out,
       not_74_out, not_75_out, not_76_out, not_77_out, not_78_out, not_79_out, not_80_out, not_81_out,
       not_82_out, not_83_out, not_84_out, not_85_out, not_86_out, not_87_out, not_88_out, not_89_out,
       not_90_out, not_91_out, not_92_out, not_93_out, not_94_out, not_95_out, not_96_out, not_97_out,
       not_98_out, not_99_out, not_100_out, not_101_out, not_102_out, not_103_out, not_104_out, not_105_out,
       not_106_out, not_107_out, not_108_out, not_109_out, not_110_out, not_111_out, not_112_out,
       not_113_out, not_114_out, not_115_out, not_116_out, not_117_out;

  not not_1 (not_1_out, e[0]);
  not not_2 (not_2_out, e[1]);
  not not_3 (not_3_out, e[2]);
  not not_4 (not_4_out, e[3]);
  not not_5 (not_5_out, e[4]);
  not not_6 (not_6_out, e[5]);
  not not_7 (not_7_out, e[0]);
  not not_8 (not_8_out, e[1]);
  not not_9 (not_9_out, e[2]);
  not not_10 (not_10_out, e[4]);
  not not_11 (not_11_out, e[5]);
  not not_12 (not_12_out, e[0]);
  not not_13 (not_13_out, e[1]);
  not not_14 (not_14_out, e[2]);
  not not_15 (not_15_out, e[3]);
  not not_16 (not_16_out, e[5]);
  not not_17 (not_17_out, e[0]);
  not not_18 (not_18_out, e[1]);
  not not_19 (not_19_out, e[2]);
  not not_20 (not_20_out, e[3]);
  not not_21 (not_21_out, e[4]);
  not not_22 (not_22_out, e[0]);
  not not_23 (not_23_out, e[1]);
  not not_24 (not_24_out, e[2]);
  not not_25 (not_25_out, e[4]);
  and and_1 (_0, not_1_out, not_2_out, not_3_out, not_4_out, not_5_out, not_6_out, en);
  and and_2 (_8, not_7_out, not_8_out, not_9_out, e[3], not_10_out, not_11_out, en);
  and and_3 (_16, not_12_out, not_13_out, not_14_out, not_15_out, e[4], not_16_out, en);
  and and_4 (_32, not_17_out, not_18_out, not_19_out, not_20_out, not_21_out, e[5], en);
  and and_5 (_40, not_22_out, not_23_out, not_24_out, e[3], not_25_out, e[5], en);
  and and_6 (_9, e[0], not_26_out, not_27_out, e[3], not_28_out, not_29_out, en);
  not not_26 (not_26_out, e[1]);
  not not_27 (not_27_out, e[2]);
  not not_28 (not_28_out, e[4]);
  not not_29 (not_29_out, e[5]);
  and and_7 (_33, e[0], not_30_out, not_31_out, not_32_out, not_33_out, e[5], en);
  not not_30 (not_30_out, e[1]);
  not not_31 (not_31_out, e[2]);
  not not_32 (not_32_out, e[3]);
  not not_33 (not_33_out, e[4]);
  not not_34 (not_34_out, e[0]);
  not not_35 (not_35_out, e[2]);
  not not_36 (not_36_out, e[3]);
  not not_37 (not_37_out, e[4]);
  not not_38 (not_38_out, e[5]);
  not not_39 (not_39_out, e[0]);
  not not_40 (not_40_out, e[2]);
  not not_41 (not_41_out, e[4]);
  not not_42 (not_42_out, e[5]);
  not not_43 (not_43_out, e[0]);
  not not_44 (not_44_out, e[2]);
  not not_45 (not_45_out, e[3]);
  not not_46 (not_46_out, e[5]);
  not not_47 (not_47_out, e[0]);
  not not_48 (not_48_out, e[2]);
  not not_49 (not_49_out, e[3]);
  not not_50 (not_50_out, e[4]);
  not not_51 (not_51_out, e[0]);
  not not_52 (not_52_out, e[2]);
  not not_53 (not_53_out, e[4]);
  and and_8 (_2, not_34_out, e[1], not_35_out, not_36_out, not_37_out, not_38_out, en);
  and and_9 (_10, not_39_out, e[1], not_40_out, e[3], not_41_out, not_42_out, en);
  and and_10 (_18, not_43_out, e[1], not_44_out, not_45_out, e[4], not_46_out, en);
  and and_11 (_34, not_47_out, e[1], not_48_out, not_49_out, not_50_out, e[5], en);
  and and_12 (_42, not_51_out, e[1], not_52_out, e[3], not_53_out, e[5], en);
  not not_54 (not_54_out, e[2]);
  not not_55 (not_55_out, e[3]);
  not not_56 (not_56_out, e[4]);
  not not_57 (not_57_out, e[5]);
  not not_58 (not_58_out, e[2]);
  not not_59 (not_59_out, e[4]);
  not not_60 (not_60_out, e[5]);
  not not_61 (not_61_out, e[2]);
  not not_62 (not_62_out, e[3]);
  not not_63 (not_63_out, e[4]);
  not not_64 (not_64_out, e[2]);
  not not_65 (not_65_out, e[4]);
  and and_13 (_3, e[0], e[1], not_54_out, not_55_out, not_56_out, not_57_out, en);
  and and_14 (_11, e[0], e[1], not_58_out, e[3], not_59_out, not_60_out, en);
  and and_15 (_35, e[0], e[1], not_61_out, not_62_out, not_63_out, e[5], en);
  and and_16 (_43, e[0], e[1], not_64_out, e[3], not_65_out, e[5], en);
  not not_66 (not_66_out, e[0]);
  not not_67 (not_67_out, e[1]);
  not not_68 (not_68_out, e[3]);
  not not_69 (not_69_out, e[4]);
  not not_70 (not_70_out, e[5]);
  not not_71 (not_71_out, e[0]);
  not not_72 (not_72_out, e[1]);
  not not_73 (not_73_out, e[4]);
  not not_74 (not_74_out, e[5]);
  not not_75 (not_75_out, e[0]);
  not not_76 (not_76_out, e[1]);
  not not_77 (not_77_out, e[2]);
  not not_78 (not_78_out, e[5]);
  not not_79 (not_79_out, e[0]);
  not not_80 (not_80_out, e[1]);
  not not_81 (not_81_out, e[3]);
  not not_82 (not_82_out, e[4]);
  and and_17 (_4, not_66_out, not_67_out, e[2], not_68_out, not_69_out, not_70_out, en);
  and and_18 (_12, not_71_out, not_72_out, e[2], e[3], not_73_out, not_74_out, en);
  and and_19 (_24, not_75_out, not_76_out, not_77_out, e[3], e[4], not_78_out, en);
  and and_20 (_36, not_79_out, not_80_out, e[2], not_81_out, not_82_out, e[5], en);
  and and_21 (_5, e[0], not_83_out, e[2], not_84_out, not_85_out, not_86_out, en);
  not not_83 (not_83_out, e[1]);
  not not_84 (not_84_out, e[3]);
  not not_85 (not_85_out, e[4]);
  not not_86 (not_86_out, e[5]);
  and and_22 (_13, e[0], not_87_out, e[2], e[3], not_88_out, not_89_out, en);
  not not_87 (not_87_out, e[1]);
  not not_88 (not_88_out, e[4]);
  not not_89 (not_89_out, e[5]);
  and and_23 (_25, e[0], not_90_out, not_91_out, e[3], e[4], not_92_out, en);
  not not_90 (not_90_out, e[1]);
  not not_91 (not_91_out, e[2]);
  not not_92 (not_92_out, e[5]);
  and and_24 (_37, e[0], not_93_out, e[2], not_94_out, not_95_out, e[5], en);
  not not_93 (not_93_out, e[1]);
  not not_94 (not_94_out, e[3]);
  not not_95 (not_95_out, e[4]);
  not not_96 (not_96_out, e[0]);
  not not_97 (not_97_out, e[3]);
  not not_98 (not_98_out, e[4]);
  not not_99 (not_99_out, e[5]);
  not not_100 (not_100_out, e[0]);
  not not_101 (not_101_out, e[4]);
  not not_102 (not_102_out, e[5]);
  not not_103 (not_103_out, e[0]);
  not not_104 (not_104_out, e[2]);
  not not_105 (not_105_out, e[5]);
  not not_106 (not_106_out, e[0]);
  not not_107 (not_107_out, e[3]);
  not not_108 (not_108_out, e[4]);
  and and_25 (_6, not_96_out, e[1], e[2], not_97_out, not_98_out, not_99_out, en);
  and and_26 (_14, not_100_out, e[1], e[2], e[3], not_101_out, not_102_out, en);
  and and_27 (_26, not_103_out, e[1], not_104_out, e[3], e[4], not_105_out, en);
  and and_28 (_38, not_106_out, e[1], e[2], not_107_out, not_108_out, e[5], en);
  not not_109 (not_109_out, e[3]);
  not not_110 (not_110_out, e[4]);
  not not_111 (not_111_out, e[5]);
  not not_112 (not_112_out, e[4]);
  not not_113 (not_113_out, e[5]);
  not not_114 (not_114_out, e[2]);
  not not_115 (not_115_out, e[5]);
  not not_116 (not_116_out, e[3]);
  not not_117 (not_117_out, e[4]);
  and and_29 (_7, e[0], e[1], e[2], not_109_out, not_110_out, not_111_out, en);
  and and_30 (_15, e[0], e[1], e[2], e[3], not_112_out, not_113_out, en);
  and and_31 (_27, e[0], e[1], not_114_out, e[3], e[4], not_115_out, en);
  and and_32 (_39, e[0], e[1], e[2], not_116_out, not_117_out, e[5], en);

  // Notes on the sheet:
  //   Décodeur
endmodule

/* Test case:
e en 43 42 40 39 38 37 36 35 34 33 32 27 26 25 24 18 16 15 14 13 12 11 10 9 8 7 6 5 4 3 2 0
0 0  bits(32,0)
0 1  bits(32,1)
repeat(15) (n+2) 0 bits(32,0)
repeat(15) (n+2) 1  bits(32,1<<(n+1))
18 0  bits(32,0)
18 1  bits(32,1<<16)
repeat(4) (n+24) 0 bits(32,0)
repeat(4) (n+24) 1  bits(32,1<<(n+17))

repeat(9) (n+32) 0 bits(32,0)
repeat(9) (n+32) 1  bits(32,1<<(n+21))


repeat(2) (n+42) 0 bits(32,0)
repeat(2) (n+42) 1  bits(32,1<<(n+30))
*/
