// Digital circuit encodeur16.dig as structural Verilog
module encodeur16 (
  input  _0,
  input  _1,
  input  _2,
  input  _3,
  input  _4,
  input  _5,
  input  _6,
  input  _7,
  input  _8,
  input  _9,
  input  _10,
  input  _11,
  input  _12,
  input  _13,
  input  _14,
  input  _15,
  output [3:0] s
);

  or or_1 (s[0], _1, _3, _5, _7, _9, _11, _13, _15);
  or or_2 (s[1], _2, _3, _6, _7, _10, _11, _14, _15);
  or or_3 (s[2], _4, _5, _6, _7, _12, _13, _14, _15);
  or or_4 (s[3], _8, _9, _10, _11, _12, _13, _14, _15);

  // Other names for the same wires on the sheet: e_0 = _0; e_1 = _1; e_2 = _2; e_3 = _3; e_4 = _4; e_5 = _5; e_6 = _6;
  //   e_7 = _7; e_8 = _8; e_9 = _9; e_10 = _10; e_11 = _11; e_12 = _12; e_13 = _13; e_14 = _14; e_15 = _15;
  //   s_0 = s[0]; s_1 = s[1]; s_2 = s[2]; s_3 = s[3]

  // Notes on the sheet:
  //   _8: default 1
  //   Encodeur 16bits
endmodule

/* Test case:
 15 14 13 12 11 10 9 8 7 6 5 4 3 2 1 0 s
repeat(16) bits(16,1<<n) (n)
*/
